// Logisim project 4X4_MEMORY_READ_WRITE.circ as structural Verilog
module main (
);

  wire CLEAR_p1, n7402_1_pin1, n7402_1_pin4, n7402_1_pin10, n7402_1_pin13, n74175_1_pin2, n74175_1_pin7,
       n74175_1_pin10, n74175_1_pin15, n74175_2_pin2, n74175_2_pin7, n74175_2_pin10, n74175_2_pin15,
       n74175_3_pin2, n74175_3_pin7, n74175_3_pin10, n74175_3_pin15, n74175_4_pin2, n74175_4_pin7,
       n74175_4_pin10, n74175_4_pin15, RW_p1;
  wire [1:0] dipswitch_2_sw2;
  wire [2:0] n7432_1_pin14;
  wire [3:0] dipswitch_1_sw4, n7408_1_pin11, n7432_1_pin11, n7432_1_pin12, n74244_1_pin9;

  Clock clock_1 (.out(n7432_1_pin14[2]));
  LED led_1 (.in(n74244_1_pin9[3]));
  // DipSwitch #(.number(1)) CLEAR: pin names not known; wires that end beside it: CLEAR_p1
  DipSwitch #(.number(4)) dipswitch_1 (
    .sw1(dipswitch_1_sw4[3]), .sw2(dipswitch_1_sw4[2]), .sw3(dipswitch_1_sw4[1]), .sw4(dipswitch_1_sw4[0]));
  // DipSwitch #(.number(1)) RW: pin names not known; wires that end beside it: RW_p1
  LED led_2 (.in(n74244_1_pin9[2]));
  LED led_3 (.in(n74244_1_pin9[1]));
  LED led_4 (.in(n74244_1_pin9[0]));
  DipSwitch #(.number(2)) dipswitch_2 (.sw1(dipswitch_2_sw2[1]), .sw2(dipswitch_2_sw2[0]));
  _7432 #(.VccGndPorts("true")) u_7432_1 (
    .pin1(CLEAR_p1), .pin2(n7432_1_pin12[2]), .pin3(n7432_1_pin11[2]), .pin4(CLEAR_p1),
    .pin5(n7432_1_pin12[3]), .pin6(n7432_1_pin11[3]), .pin7(n7432_1_pin14[1]), .pin14(n7432_1_pin14[0]),
    .pin13(CLEAR_p1), .pin12(n7432_1_pin12[0]), .pin11(n7432_1_pin11[0]), .pin10(CLEAR_p1),
    .pin9(n7432_1_pin12[1]), .pin8(n7432_1_pin11[1]));
  _74139 #(.VccGndPorts("true")) u_74139_1 (
    .pin1(n7432_1_pin14[1]), .pin2(dipswitch_2_sw2[0]), .pin3(dipswitch_2_sw2[1]), .pin4(n7432_1_pin12[0]),
    .pin5(n7432_1_pin12[1]), .pin6(n7432_1_pin12[2]), .pin7(n7432_1_pin12[3]), .pin8(n7432_1_pin14[1]),
    .pin16(n7432_1_pin14[0]));  // open: pin15, pin14, pin13, pin12, pin11, pin10, pin9
  _7402 #(.VccGndPorts("true")) u_7402_1 (
    .pin1(n7402_1_pin1), .pin2(n7432_1_pin12[3]), .pin3(n7432_1_pin14[2]), .pin4(n7402_1_pin4),
    .pin5(n7432_1_pin12[2]), .pin6(n7432_1_pin14[2]), .pin7(n7432_1_pin14[1]), .pin14(n7432_1_pin14[0]),
    .pin13(n7402_1_pin13), .pin12(n7432_1_pin12[0]), .pin11(n7432_1_pin14[2]), .pin10(n7402_1_pin10),
    .pin9(n7432_1_pin12[1]), .pin8(n7432_1_pin14[2]));
  _7408 #(.VccGndPorts("true")) u_7408_1 (
    .pin1(n7402_1_pin4), .pin2(RW_p1), .pin3(n7408_1_pin11[2]), .pin4(n7402_1_pin1), .pin5(RW_p1),
    .pin6(n7408_1_pin11[3]), .pin7(n7432_1_pin14[1]), .pin14(n7432_1_pin14[0]), .pin13(n7402_1_pin13),
    .pin12(RW_p1), .pin11(n7408_1_pin11[0]), .pin10(n7402_1_pin10), .pin9(RW_p1), .pin8(n7408_1_pin11[1]));
  _74175 #(.VccGndPorts("true")) u_74175_1 (
    .pin1(n7432_1_pin11[3]), .pin2(n74175_1_pin2), .pin4(dipswitch_1_sw4[0]), .pin5(dipswitch_1_sw4[1]),
    .pin7(n74175_1_pin7), .pin8(n7432_1_pin14[1]), .pin16(n7432_1_pin14[0]), .pin15(n74175_1_pin15),
    .pin13(dipswitch_1_sw4[3]), .pin12(dipswitch_1_sw4[2]), .pin10(n74175_1_pin10), .pin9(n7408_1_pin11[3]));  // open: pin3, pin6, pin14, pin11
  _74175 #(.VccGndPorts("true")) u_74175_2 (
    .pin1(n7432_1_pin11[0]), .pin2(n74175_2_pin2), .pin4(dipswitch_1_sw4[0]), .pin5(dipswitch_1_sw4[1]),
    .pin7(n74175_2_pin7), .pin8(n7432_1_pin14[1]), .pin16(n7432_1_pin14[0]), .pin15(n74175_2_pin15),
    .pin13(dipswitch_1_sw4[3]), .pin12(dipswitch_1_sw4[2]), .pin10(n74175_2_pin10), .pin9(n7408_1_pin11[0]));  // open: pin3, pin6, pin14, pin11
  _74175 #(.VccGndPorts("true")) u_74175_3 (
    .pin1(n7432_1_pin11[1]), .pin2(n74175_3_pin2), .pin4(dipswitch_1_sw4[0]), .pin5(dipswitch_1_sw4[1]),
    .pin7(n74175_3_pin7), .pin8(n7432_1_pin14[1]), .pin16(n7432_1_pin14[0]), .pin15(n74175_3_pin15),
    .pin13(dipswitch_1_sw4[3]), .pin12(dipswitch_1_sw4[2]), .pin10(n74175_3_pin10), .pin9(n7408_1_pin11[1]));  // open: pin3, pin6, pin14, pin11
  _74175 #(.VccGndPorts("true")) u_74175_4 (
    .pin1(n7432_1_pin11[2]), .pin2(n74175_4_pin2), .pin4(dipswitch_1_sw4[0]), .pin5(dipswitch_1_sw4[1]),
    .pin7(n74175_4_pin7), .pin8(n7432_1_pin14[1]), .pin16(n7432_1_pin14[0]), .pin15(n74175_4_pin15),
    .pin13(dipswitch_1_sw4[3]), .pin12(dipswitch_1_sw4[2]), .pin10(n74175_4_pin10), .pin9(n7408_1_pin11[2]));  // open: pin3, pin6, pin14, pin11
  _74244 #(.VccGndPorts("true")) u_74244_1 (
    .pin1(n7432_1_pin12[2]), .pin2(n74175_4_pin2), .pin3(n74244_1_pin9[3]), .pin4(n74175_4_pin7),
    .pin5(n74244_1_pin9[2]), .pin6(n74175_4_pin10), .pin7(n74244_1_pin9[1]), .pin8(n74175_4_pin15),
    .pin9(n74244_1_pin9[0]), .pin10(n7432_1_pin14[1]), .pin20(n7432_1_pin14[0]), .pin19(n7432_1_pin12[3]),
    .pin18(n74244_1_pin9[0]), .pin17(n74175_1_pin15), .pin16(n74244_1_pin9[1]), .pin15(n74175_1_pin10),
    .pin14(n74244_1_pin9[2]), .pin13(n74175_1_pin7), .pin12(n74244_1_pin9[3]), .pin11(n74175_1_pin2));
  _74244 #(.VccGndPorts("true")) u_74244_2 (
    .pin1(n7432_1_pin12[0]), .pin2(n74175_2_pin2), .pin3(n74244_1_pin9[3]), .pin4(n74175_2_pin7),
    .pin5(n74244_1_pin9[2]), .pin6(n74175_2_pin10), .pin7(n74244_1_pin9[1]), .pin8(n74175_2_pin15),
    .pin9(n74244_1_pin9[0]), .pin10(n7432_1_pin14[1]), .pin20(n7432_1_pin14[0]), .pin19(n7432_1_pin12[1]),
    .pin18(n74244_1_pin9[0]), .pin17(n74175_3_pin15), .pin16(n74244_1_pin9[1]), .pin15(n74175_3_pin10),
    .pin14(n74244_1_pin9[2]), .pin13(n74175_3_pin7), .pin12(n74244_1_pin9[3]), .pin11(n74175_3_pin2));
  // also tied to GND on the sheet: n7432_1_pin14[1]
  // also tied to VCC on the sheet: n7432_1_pin14[0]
endmodule
